# Fritzing sketch sketch_p8 (saved by Fritzing 0.9.9b)

parts:
  Componente1 = Arduino Uno (Rev3)
  M1 = MakerFocus MAX30102
  OLED2 = OLED 128x64 I2C Monochrome Display  # not connected

nets:
  N1: Componente1.A4/SDA, M1.SCL
  N2: Componente1.A5/SCL, M1.SDA
  5V: Componente1.5V, M1.VIN
  GND: Componente1.GND, M1.GND

custom parts:
  MakerFocus MAX30102: Oximeter module using the MAX30102 chip. As usual, if you want the mounting holes in pcb, you need to drag a hole over the pad in silkscreen to actually drill the hole (by default they are not drilled)
